// Logisim project cpu.circ as structural Verilog: 14 circuits, main circuit main
module main (
  input  reset
);

  wire and_1_out, and_2_out, and_3_out, comparator_1_eq, comparator_2_eq, comparator_3_eq, not_1_out,
       not_2_out, or_1_out, signal_1_beqpc, signal_1_bnepc, signal_1_disp, signal_1_none, signal_1_rmem,
       signal_1_smem, signal_1_wreg;
  wire [1:0] bitselector_3_out, bitselector_4_out, bitselector_5_out, bitselector_7_out, multiplexer_1_out;
  wire [3:0] bitselector_2_out;
  wire [7:0] bitselector_6_out;
  wire [11:0] bitselector_1_out;
  wire [15:0] adder_1_out, alu_1_output, bit_extender_1_out, controlled_buffer_1_out,
       controlled_buffer_2_out, controlled_buffer_3_out, controlled_buffer_5_out, demultiplexer_1_out0,
       demultiplexer_1_out1, demultiplexer_1_out2, demultiplexer_1_out3, multiplexer_2_out, pc_1_instroutput,
       ram_unit_1_dataout, registers_1_busa, registers_1_busb, rom_1_data;

  PC pc_1 (
    .Wenable(1'b1), .reset(reset), .ifJ(comparator_2_eq), .jaddress(bit_extender_1_out),
    .perStep(multiplexer_2_out), .instrOutput(pc_1_instroutput));
  ROM #(.addrWidth(16), .dataWidth(16)) rom_1 (.addr(pc_1_instroutput), .data(rom_1_data));  // open: sel
  BitSelector #(.width(16), .group(12)) bitselector_1 (.in(rom_1_data), .out(bitselector_1_out), .sel(1'b0));
  BitSelector #(.width(16), .group(4)) bitselector_2 (.in(rom_1_data), .out(bitselector_2_out), .sel(2'b11));
  assign bit_extender_1_out = {{4{1'b0}}, bitselector_1_out};  // Bit_Extender bit_extender_1
  assign controlled_buffer_1_out = not_1_out ? rom_1_data : 16'bz;  // Controlled_Buffer controlled_buffer_1
  not not_1 (not_1_out, comparator_2_eq);
  Comparator #(.width(4)) comparator_1 (.a(bitselector_2_out), .b(4'b0000), .eq(comparator_1_eq));  // open: gt, lt
  SIgnal signal_1 (
    .opcode(bitselector_2_out), .disp(signal_1_disp), .wreg(signal_1_wreg), .Rmem(signal_1_rmem),
    .Smem(signal_1_smem), .beqpc(signal_1_beqpc), .bnepc(signal_1_bnepc), .none(signal_1_none));
  Comparator #(.width(4)) comparator_2 (.a(bitselector_2_out), .b(4'b1000), .eq(comparator_2_eq));  // open: gt, lt
  BitSelector #(.width(16), .group(2)) bitselector_3 (
    .in(controlled_buffer_1_out), .out(bitselector_3_out), .sel(3'b011));
  Multiplexer #(.width(2), .enable("false")) multiplexer_1 (
    .in0(bitselector_5_out), .in1(bitselector_3_out), .out(multiplexer_1_out), .sel(comparator_1_eq));
  BitSelector #(.width(16), .group(2)) bitselector_4 (
    .in(controlled_buffer_1_out), .out(bitselector_4_out), .sel(3'b101));
  Registers registers_1 (
    .busW(controlled_buffer_2_out), .WEnable(1'b1), .RW(multiplexer_1_out), .RA(bitselector_4_out),
    .RB(bitselector_5_out), .Reset(reset), .busA(registers_1_busa), .busB(registers_1_busb));
  BitSelector #(.width(16), .group(2)) bitselector_5 (
    .in(controlled_buffer_1_out), .out(bitselector_5_out), .sel(3'b100));
  Comparator #(.width(16)) comparator_3 (
    .a(registers_1_busb), .b(registers_1_busa), .eq(comparator_3_eq));  // open: gt, lt
  BitSelector #(.width(16), .group(8)) bitselector_6 (
    .in(controlled_buffer_1_out), .out(bitselector_6_out), .sel(1'b0));
  assign controlled_buffer_2_out = signal_1_wreg ? alu_1_output : 16'bz;  // Controlled_Buffer controlled_buffer_2
  assign controlled_buffer_3_out = signal_1_disp ? registers_1_busa : 16'bz;  // Controlled_Buffer controlled_buffer_3
  and and_1 (and_1_out, signal_1_beqpc, comparator_3_eq);
  not not_2 (not_2_out, comparator_3_eq);
  and and_2 (and_2_out, not_2_out, signal_1_bnepc);
  ALU alu_1 (
    .opnum1(registers_1_busa), .opnum2(registers_1_busb), .imm(bitselector_6_out),
    .opcode(bitselector_2_out), .intro(controlled_buffer_1_out), .in_6(reset), .\output (alu_1_output));
  or or_1 (or_1_out, and_1_out, and_2_out);
  Demultiplexer #(.select(2), .width(16)) demultiplexer_1 (
    .out0(demultiplexer_1_out0), .out1(demultiplexer_1_out1), .out2(demultiplexer_1_out2),
    .out3(demultiplexer_1_out3), .in(controlled_buffer_3_out), .sel(bitselector_7_out));  // open: en
  assign controlled_buffer_2_out = signal_1_rmem ? ram_unit_1_dataout : 16'bz;  // Controlled_Buffer controlled_buffer_4
  and and_3 (and_3_out, or_1_out, 1'b1);
  display display_1 (
    .disp_0(demultiplexer_1_out0), .disp_1(demultiplexer_1_out1), .disp_2(demultiplexer_1_out2),
    .disp_3(demultiplexer_1_out3), .whichw(bitselector_7_out), .WEnable(signal_1_disp), .reset(reset));
  RAM_Unit ram_unit_1 (
    .DataIn(registers_1_busb), .Address(controlled_buffer_5_out), .Reset(reset), .WEnable(signal_1_smem),
    .DataOut(ram_unit_1_dataout));
  Adder #(.width(16)) adder_1 (.a(alu_1_output), .b(16'h1), .out(adder_1_out));  // open: cin, cout
  BitSelector #(.width(16), .group(2)) bitselector_7 (.in(alu_1_output), .out(bitselector_7_out), .sel(3'b000));
  assign controlled_buffer_5_out = signal_1_rmem ? alu_1_output : 16'bz;  // Controlled_Buffer controlled_buffer_5
  assign controlled_buffer_5_out = signal_1_smem ? alu_1_output : 16'bz;  // Controlled_Buffer controlled_buffer_6
  Multiplexer #(.width(16), .enable("false")) multiplexer_2 (
    .in0(16'h1), .in1(adder_1_out), .out(multiplexer_2_out), .sel(and_3_out));

  // Notes on the sheet:
  //   contents of rom_1 (hex, n*v repeats v):
  //   4002 4503 4a00 7800 7901 3 543 6800 6901 9908 fc3 6e02 882 7e02 a83 4f01 743 a9f7 95ff
  //   opcode
  //   R-format
  //   控制信号
  //   J-format
  //   wreg signal
  //   disp signal
  //   w&R mem sig
  //   beq signal
  //   bne signal
  //   Rd
  //   busW
  //   RS
  //   RT
  //   busA
  //   busB
  //   immediate
  //   funct
  //   ALU
  //   display
  //   RAM
endmodule

module RAM_Unit (
  input  [15:0] DataIn,
  input  [15:0] Address,
  input  Reset,
  input  WEnable,
  output [15:0] DataOut
);

  wire clock_2_out, clock_3_out, CLock_out, multiplexer_1_out, not_1_out, not_2_out, xor_1_out;

  assign DataOut = multiplexer_1_out ? DataIn : 16'bz;  // Controlled_Buffer Control_Buffer
  not not_1 (not_1_out, CLock_out);
  not not_2 (not_2_out, multiplexer_1_out);
  Clock CLock (.out(CLock_out));
  RAM #(.addrWidth(16), .dataWidth(16)) ram_1 (
    .addr(Address), .data(DataOut), .clk(not_1_out), .ld(not_2_out), .clr(Reset));  // open: sel
  Clock #(.highDuration(4), .lowDuration(4)) clock_2 (.out(clock_2_out));
  Clock #(.highDuration(2), .lowDuration(6)) clock_3 (.out(clock_3_out));
  Multiplexer #(.enable("false")) multiplexer_1 (.in0(1'b0), .in1(WEnable), .out(multiplexer_1_out), .sel(xor_1_out));
  xor xor_1 (xor_1_out, clock_2_out, clock_3_out);
endmodule

// registers
module Registers (
  input  [1:0] RW,
  input  [1:0] RA,
  input  [1:0] RB,
  input  WEnable,
  input  [15:0] busW,
  input  Reset,
  output [15:0] busA,
  output [15:0] busB
);

  wire clock_1_out, clock_2_out, clock_3_out, demultiplexer_1_out0, demultiplexer_1_out1,
       demultiplexer_1_out2, demultiplexer_1_out3, multiplexer_1_out, xor_1_out;
  wire [15:0] demultiplexer_2_out0, demultiplexer_2_out1, demultiplexer_2_out2, demultiplexer_2_out3,
       register_1_q, register_2_q, register_3_q, register_4_q;

  Clock #(.highDuration(4), .lowDuration(4)) clock_1 (.out(clock_1_out));
  Clock #(.highDuration(2), .lowDuration(6)) clock_2 (.out(clock_2_out));
  Multiplexer #(.enable("false")) multiplexer_1 (.in0(1'b0), .in1(WEnable), .out(multiplexer_1_out), .sel(xor_1_out));
  xor xor_1 (xor_1_out, clock_1_out, clock_2_out);
  Clock clock_3 (.out(clock_3_out));
  Demultiplexer #(.select(2)) demultiplexer_1 (
    .out0(demultiplexer_1_out0), .out1(demultiplexer_1_out1), .out2(demultiplexer_1_out2),
    .out3(demultiplexer_1_out3), .in(multiplexer_1_out), .sel(RW));  // open: en
  Demultiplexer #(.select(2), .width(16)) demultiplexer_2 (
    .out0(demultiplexer_2_out0), .out1(demultiplexer_2_out1), .out2(demultiplexer_2_out2),
    .out3(demultiplexer_2_out3), .in(busW), .sel(RW));  // open: en
  Register #(.width(16)) register_1 (
    .D(demultiplexer_2_out0), .en(demultiplexer_1_out0), .Q(register_1_q), .clk(clock_3_out), .clr(Reset));
  Register #(.width(16)) register_2 (
    .D(demultiplexer_2_out1), .en(demultiplexer_1_out1), .Q(register_2_q), .clk(clock_3_out), .clr(Reset));
  Multiplexer #(.select(2), .width(16), .enable("false")) multiplexer_2 (
    .in0(register_1_q), .in1(register_2_q), .in2(register_3_q), .in3(register_4_q), .out(busA), .sel(RA));
  Register #(.width(16)) register_3 (
    .D(demultiplexer_2_out2), .en(demultiplexer_1_out2), .Q(register_3_q), .clk(clock_3_out), .clr(Reset));
  Register #(.width(16)) register_4 (
    .D(demultiplexer_2_out3), .en(demultiplexer_1_out3), .Q(register_4_q), .clk(clock_3_out), .clr(Reset));
  Multiplexer #(.select(2), .width(16), .enable("false")) multiplexer_3 (
    .in0(register_1_q), .in1(register_2_q), .in2(register_3_q), .in3(register_4_q), .out(busB), .sel(RB));
endmodule

module ALU_R (
  input  [2:0] funct,
  input  [15:0] RS,
  input  [15:0] RT,
  output [15:0] \output 
);

  wire comparator_1_lt;
  wire [3:0] bit_extender_1_out, bit_extender_2_out, bit_extender_3_out;
  wire [15:0] adder_1_out, and_1_out, bit_extender_4_out, or_1_out, shifter_1_out, shifter_2_out,
       shifter_3_out, subtractor_1_out;

  Bit_Extender #(.in_width(16), .out_width(4)) bit_extender_1 (.in(RT), .out(bit_extender_1_out));
  Bit_Extender #(.in_width(16), .out_width(4)) bit_extender_2 (.in(RT), .out(bit_extender_2_out));
  Bit_Extender #(.in_width(16), .out_width(4)) bit_extender_3 (.in(RS), .out(bit_extender_3_out));
  assign or_1_out = RS | RT;  // OR_Gate or_1, 16 bits wide
  assign and_1_out = RS & RT;  // AND_Gate and_1, 16 bits wide
  Adder #(.width(16)) adder_1 (.a(RS), .b(RT), .out(adder_1_out));  // open: cin, cout
  Subtractor #(.width(16)) subtractor_1 (.a(RS), .b(RT), .out(subtractor_1_out));  // open: bin, bout
  Shifter #(.width(16)) shifter_1 (.in(RS), .\dist (bit_extender_1_out), .out(shifter_1_out));
  Shifter #(.width(16), .shift("lr")) shifter_2 (.in(RT), .\dist (bit_extender_2_out), .out(shifter_2_out));
  Shifter #(.width(16), .shift("ar")) shifter_3 (.in(RS), .\dist (bit_extender_3_out), .out(shifter_3_out));
  Comparator #(.width(16)) comparator_1 (.a(RS), .b(RT), .lt(comparator_1_lt));  // open: gt, eq
  assign bit_extender_4_out = {{15{1'b0}}, comparator_1_lt};  // Bit_Extender bit_extender_4
  Multiplexer #(.select(3), .width(16), .enable("false")) multiplexer_1 (
    .in0(or_1_out), .in1(and_1_out), .in2(adder_1_out), .in3(subtractor_1_out), .in4(shifter_1_out),
    .in5(shifter_2_out), .in6(shifter_3_out), .in7(bit_extender_4_out), .out(\output ), .sel(funct));

  // Notes on the sheet:
  //   or
  //   and
  //   add
  //   sub
  //   sllv
  //   srlv
  //   srav
  //   slt
endmodule

module PC (
  input  [15:0] jaddress,
  input  ifJ,
  input  [15:0] perStep,
  input  Wenable,
  input  reset,
  output [15:0] instrOutput
);

  wire clock_1_out, not_1_out;
  wire [15:0] adder_1_out, multiplexer_1_out;

  Clock #(.highDuration(4), .lowDuration(4)) clock_1 (.out(clock_1_out));
  not not_1 (not_1_out, clock_1_out);
  Register #(.width(16)) register_1 (
    .D(multiplexer_1_out), .en(Wenable), .Q(instrOutput), .clk(not_1_out), .clr(reset));
  Multiplexer #(.width(16), .enable("false")) multiplexer_1 (
    .in0(adder_1_out), .in1(jaddress), .out(multiplexer_1_out), .sel(ifJ));
  Adder #(.width(16)) adder_1 (.a(instrOutput), .b(perStep), .out(adder_1_out));  // open: cin, cout
endmodule

module ALU (
  input  [3:0] opcode,
  input  [15:0] intro,
  input  [15:0] opnum1,
  input  [15:0] opnum2,
  input  [7:0] imm,
  input  in_6,
  output [15:0] \output 
);

  wire clock_1_out, clock_2_out, xor_1_out;
  wire [2:0] bitselector_1_out;
  wire [15:0] adder_1_out, adder_2_out, adder_3_out, alu_r_1_output, and_1_out, bit_extender_1_out,
       bit_extender_2_out, bit_extender_3_out, bit_extender_4_out, bit_extender_5_out, bit_extender_6_out,
       bit_extender_7_out, bit_extender_8_out, bit_extender_9_out, multiplexer_1_out, or_1_out,
       shifter_1_out, undriven;

  assign bit_extender_1_out = {{8{1'b0}}, imm};  // Bit_Extender bit_extender_1
  assign bit_extender_2_out = {{8{1'b0}}, imm};  // Bit_Extender bit_extender_2
  assign bit_extender_3_out = {{8{1'b0}}, imm};  // Bit_Extender bit_extender_3
  assign bit_extender_4_out = {{8{imm[7]}}, imm};  // Bit_Extender bit_extender_4
  assign bit_extender_5_out = {{8{1'b0}}, imm};  // Bit_Extender bit_extender_5
  assign bit_extender_6_out = {{8{imm[7]}}, imm};  // Bit_Extender bit_extender_6
  assign bit_extender_7_out = {{8{imm[7]}}, imm};  // Bit_Extender bit_extender_7
  assign bit_extender_8_out = {{8{imm[7]}}, imm};  // Bit_Extender bit_extender_8
  assign bit_extender_9_out = {{8{imm[7]}}, imm};  // Bit_Extender bit_extender_9
  BitSelector #(.width(16), .group(3)) bitselector_1 (.in(intro), .out(bitselector_1_out), .sel(3'b000));
  ALU_R alu_r_1 (.RS(opnum1), .RT(opnum2), .funct(bitselector_1_out), .\output (alu_r_1_output));
  Adder #(.width(16)) adder_1 (.a(opnum1), .b(bit_extender_6_out), .out(adder_1_out));  // open: cin, cout
  Adder #(.width(16)) adder_2 (.a(opnum1), .b(bit_extender_7_out), .out(adder_2_out));  // open: cin, cout
  Shifter #(.width(16)) shifter_1 (.in(bit_extender_2_out), .\dist (4'b1000), .out(shifter_1_out));
  assign or_1_out = opnum1 | bit_extender_3_out;  // OR_Gate or_1, 16 bits wide
  Adder #(.width(16)) adder_3 (.a(opnum1), .b(bit_extender_4_out), .out(adder_3_out));  // open: cin, cout
  assign and_1_out = opnum1 & bit_extender_5_out;  // AND_Gate and_1, 16 bits wide
  Multiplexer #(.select(4), .width(16), .enable("false")) multiplexer_1 (
    .in0(alu_r_1_output), .in1(bit_extender_1_out), .in2(shifter_1_out), .in3(or_1_out), .in4(adder_3_out),
    .in5(and_1_out), .in6(adder_1_out), .in7(adder_2_out), .in8(undriven), .in9(bit_extender_8_out),
    .in10(bit_extender_9_out), .out(multiplexer_1_out), .sel(opcode));  // open: in11, in12, in13, in14, in15
  Clock #(.highDuration(4), .lowDuration(4)) clock_1 (.out(clock_1_out));
  Clock #(.highDuration(6), .lowDuration(2)) clock_2 (.out(clock_2_out));
  Register #(.width(16)) register_1 (.D(multiplexer_1_out), .en(1'b1), .Q(\output ), .clk(xor_1_out), .clr(in_6));
  xor xor_1 (xor_1_out, clock_1_out, clock_2_out);

  // Notes on the sheet:
  //   lw
  //   sw
  //   beq
  //   bne
  //   R-format
  //   disp
  //   ori
  //   addi
  //   andj
  //   lui
endmodule

module SIgnal (
  input  [3:0] opcode,
  output disp,
  output wreg,
  output Rmem,
  output Smem,
  output beqpc,
  output bnepc,
  output none
);

  wire demultiplexer_1_out0, demultiplexer_1_out2, demultiplexer_1_out3, demultiplexer_1_out4,
       demultiplexer_1_out5, demultiplexer_1_out8, demultiplexer_1_out11;

  Demultiplexer #(.select(4)) demultiplexer_1 (
    .out0(demultiplexer_1_out0), .out1(disp), .out2(demultiplexer_1_out2), .out3(demultiplexer_1_out3),
    .out4(demultiplexer_1_out4), .out5(demultiplexer_1_out5), .out6(Rmem), .out7(Smem),
    .out8(demultiplexer_1_out8), .out9(beqpc), .out10(bnepc), .out11(demultiplexer_1_out11), .in(1'b1),
    .sel(opcode));  // open: out12, out13, out14, out15, en
  or or_1 (none, demultiplexer_1_out8, demultiplexer_1_out11);
  or or_2 (wreg, demultiplexer_1_out0, demultiplexer_1_out2, demultiplexer_1_out3, demultiplexer_1_out4, demultiplexer_1_out5);
endmodule

module Converter (
  input  [7:0] in_1,
  output out_2,
  output out_3,
  output out_4,
  output out_5,
  output out_6,
  output out_7,
  output out_8,
  output out_9
);

  wire and_1_out, or_1_out;
  wire [7:0] multiplexer_1_out, multiplexer_2_out;

  Multiplexer #(.select(4), .width(8), .enable("false")) multiplexer_1 (
    .in0(8'h77), .in1(8'h41), .in2(8'h3b), .in3(8'h6b), .in4(8'h4d), .in5(8'h6e), .in6(8'h7e), .in7(8'h43),
    .in8(8'h7f), .in9(8'h6f), .in10(8'h5f), .in11(8'h7c), .in12(8'h36), .in13(8'h79), .in14(8'h3e),
    .in15(8'h1e), .out(multiplexer_1_out), .sel(in_1[3:0]));
  or or_1 (or_1_out, in_1[4], in_1[5], in_1[6], in_1[7]);
  Multiplexer #(.width(8), .enable("false")) multiplexer_2 (
    .in0(multiplexer_1_out), .in1(8'h9b), .out(multiplexer_2_out), .sel(or_1_out));
  and and_1 (and_1_out, in_1[0], in_1[1], in_1[2], in_1[3], in_1[4], in_1[5], in_1[6], in_1[7]);
  Multiplexer #(.width(8), .enable("false")) multiplexer_3 (
    .in0(multiplexer_2_out), .in1({8{1'b0}}), .out({out_9, out_8, out_7, out_6, out_2, out_3, out_4, out_5}),
    .sel(and_1_out));

  // Notes on the sheet:
  //   0
  //   1
  //   2
  //   3
  //   4
  //   5
  //   6
  //   7
  //   8
  //   9
  //   a
  //   b
  //   c
  //   d
  //   e
  //   f
  //   ?
endmodule

module display (
  input  [15:0] disp_0,
  input  [15:0] disp_1,
  input  reset,
  input  [15:0] disp_2,
  input  [15:0] disp_3,
  input  [1:0] whichw,
  input  WEnable
);

  wire blockbottom_1_out_5, blockbottom_1_out_6, blockbottom_1_out_7, blockbottom_1_out_8,
       blockbottom_1_out_9, blockbottom_1_out_10, blockbottom_1_out_11, blockbottom_1_out_12,
       blockbottom_1_out_13, blockbottom_1_out_14, blockbottom_1_out_15, blockbottom_1_out_16,
       blockbottom_1_out_17, blockbottom_1_out_18, blockbottom_1_out_19, blockbottom_1_out_20,
       blockbottom_2_out_5, blockbottom_2_out_6, blockbottom_2_out_7, blockbottom_2_out_8,
       blockbottom_2_out_9, blockbottom_2_out_10, blockbottom_2_out_11, blockbottom_2_out_12,
       blockbottom_2_out_13, blockbottom_2_out_14, blockbottom_2_out_15, blockbottom_2_out_16,
       blockbottom_2_out_17, blockbottom_2_out_18, blockbottom_2_out_19, blockbottom_2_out_20,
       blockbottom_3_out_5, blockbottom_3_out_6, blockbottom_3_out_7, blockbottom_3_out_8,
       blockbottom_3_out_9, blockbottom_3_out_10, blockbottom_3_out_11, blockbottom_3_out_12,
       blockbottom_3_out_13, blockbottom_3_out_14, blockbottom_3_out_15, blockbottom_3_out_16,
       blockbottom_3_out_17, blockbottom_3_out_18, blockbottom_3_out_19, blockbottom_3_out_20,
       blockbottom_4_out_5, blockbottom_4_out_6, blockbottom_4_out_7, blockbottom_4_out_8,
       blockbottom_4_out_9, blockbottom_4_out_10, blockbottom_4_out_11, blockbottom_4_out_12,
       blockbottom_4_out_13, blockbottom_4_out_14, blockbottom_4_out_15, blockbottom_4_out_16,
       blockbottom_4_out_17, blockbottom_4_out_18, blockbottom_4_out_19, blockbottom_4_out_20,
       blocktop_1_out_5, blocktop_1_out_6, blocktop_1_out_7, blocktop_1_out_8, blocktop_1_out_9,
       blocktop_1_out_10, blocktop_1_out_11, blocktop_1_out_12, blocktop_1_out_13, blocktop_1_out_14,
       blocktop_1_out_15, blocktop_1_out_16, blocktop_1_out_17, blocktop_1_out_18, blocktop_1_out_19,
       blocktop_1_out_20, blocktop_2_out_5, blocktop_2_out_6, blocktop_2_out_7, blocktop_2_out_8,
       blocktop_2_out_9, blocktop_2_out_10, blocktop_2_out_11, blocktop_2_out_12, blocktop_2_out_13,
       blocktop_2_out_14, blocktop_2_out_15, blocktop_2_out_16, blocktop_2_out_17, blocktop_2_out_18,
       blocktop_2_out_19, blocktop_2_out_20, blocktop_3_out_5, blocktop_3_out_6, blocktop_3_out_7,
       blocktop_3_out_8, blocktop_3_out_9, blocktop_3_out_10, blocktop_3_out_11, blocktop_3_out_12,
       blocktop_3_out_13, blocktop_3_out_14, blocktop_3_out_15, blocktop_3_out_16, blocktop_3_out_17,
       blocktop_3_out_18, blocktop_3_out_19, blocktop_3_out_20, blocktop_4_out_5, blocktop_4_out_6,
       blocktop_4_out_7, blocktop_4_out_8, blocktop_4_out_9, blocktop_4_out_10, blocktop_4_out_11,
       blocktop_4_out_12, blocktop_4_out_13, blocktop_4_out_14, blocktop_4_out_15, blocktop_4_out_16,
       blocktop_4_out_17, blocktop_4_out_18, blocktop_4_out_19, blocktop_4_out_20, clock_1_out, clock_2_out,
       clock_3_out, demultiplexer_1_out0, demultiplexer_1_out1, demultiplexer_1_out2, demultiplexer_1_out3,
       multiplexer_1_out, xor_1_out;
  wire [3:0] register_2_q, register_2_q_2, register_2_q_3, register_2_q_4;
  wire [7:0] bit_extender_1_out, bit_extender_2_out, bit_extender_3_out, bit_extender_4_out,
       bit_extender_5_out, bit_extender_6_out, bit_extender_7_out, bit_extender_8_out, bit_extender_9_out,
       bit_extender_10_out, bit_extender_11_out, bit_extender_12_out, bit_extender_13_out,
       bit_extender_14_out, bit_extender_15_out, bit_extender_16_out, blackbox_1_out_5, blackbox_1_out_6,
       blackbox_1_out_7, blackbox_1_out_8, blackbox_2_out_5, blackbox_2_out_6, blackbox_2_out_7,
       blackbox_2_out_8, blackbox_3_out_5, blackbox_3_out_6, blackbox_3_out_7, blackbox_3_out_8,
       blackbox_4_out_5, blackbox_4_out_6, blackbox_4_out_7, blackbox_4_out_8;
  wire [15:0] register_1_q, register_3_q, register_4_q;

  Clock clock_1 (.out(clock_1_out));
  Register #(.width(16)) register_1 (
    .D(disp_0), .en(demultiplexer_1_out0), .Q(register_1_q), .clk(clock_1_out), .clr(reset));
  Register #(.width(16)) register_2 (
    .D(disp_1), .en(demultiplexer_1_out1),
    .Q({register_2_q_4, register_2_q_3, register_2_q_2, register_2_q}), .clk(clock_1_out), .clr(reset));
  Register #(.width(16)) register_3 (
    .D(disp_2), .en(demultiplexer_1_out2), .Q(register_3_q), .clk(clock_1_out), .clr(reset));
  Register #(.width(16)) register_4 (
    .D(disp_3), .en(demultiplexer_1_out3), .Q(register_4_q), .clk(clock_1_out), .clr(reset));
  _7_Segment_Display u_7_segment_display_1 (
    .g(blocktop_1_out_5), .f(blocktop_1_out_13), .a(blocktop_1_out_14), .b(blocktop_1_out_6),
    .e(blockbottom_1_out_13), .d(blockbottom_1_out_5), .c(blockbottom_1_out_6), .dp(blockbottom_1_out_14));
  BlockBottom blockbottom_1 (
    .out_13(blockbottom_1_out_13), .out_5(blockbottom_1_out_5), .out_6(blockbottom_1_out_6),
    .out_14(blockbottom_1_out_14), .out_15(blockbottom_1_out_15), .out_7(blockbottom_1_out_7),
    .out_8(blockbottom_1_out_8), .out_16(blockbottom_1_out_16), .out_17(blockbottom_1_out_17),
    .out_9(blockbottom_1_out_9), .out_10(blockbottom_1_out_10), .out_18(blockbottom_1_out_18),
    .out_19(blockbottom_1_out_19), .out_11(blockbottom_1_out_11), .out_12(blockbottom_1_out_12),
    .out_20(blockbottom_1_out_20), .in_1(blackbox_1_out_5), .in_2(blackbox_1_out_6), .in_3(blackbox_1_out_7),
    .in_4(blackbox_1_out_8));
  assign bit_extender_1_out = {{4{1'b0}}, register_1_q[15:12]};  // Bit_Extender bit_extender_1
  _7_Segment_Display u_7_segment_display_2 (
    .g(blocktop_2_out_5), .f(blocktop_2_out_13), .a(blocktop_2_out_14), .b(blocktop_2_out_6),
    .e(blockbottom_2_out_13), .d(blockbottom_2_out_5), .c(blockbottom_2_out_6), .dp(blockbottom_2_out_14));
  BlockBottom blockbottom_2 (
    .out_13(blockbottom_2_out_13), .out_5(blockbottom_2_out_5), .out_6(blockbottom_2_out_6),
    .out_14(blockbottom_2_out_14), .out_15(blockbottom_2_out_15), .out_7(blockbottom_2_out_7),
    .out_8(blockbottom_2_out_8), .out_16(blockbottom_2_out_16), .out_17(blockbottom_2_out_17),
    .out_9(blockbottom_2_out_9), .out_10(blockbottom_2_out_10), .out_18(blockbottom_2_out_18),
    .out_19(blockbottom_2_out_19), .out_11(blockbottom_2_out_11), .out_12(blockbottom_2_out_12),
    .out_20(blockbottom_2_out_20), .in_1(blackbox_2_out_5), .in_2(blackbox_2_out_6), .in_3(blackbox_2_out_7),
    .in_4(blackbox_2_out_8));
  assign bit_extender_2_out = {{4{1'b0}}, register_3_q[15:12]};  // Bit_Extender bit_extender_2
  Demultiplexer #(.select(2)) demultiplexer_1 (
    .out0(demultiplexer_1_out0), .out1(demultiplexer_1_out1), .out2(demultiplexer_1_out2),
    .out3(demultiplexer_1_out3), .in(multiplexer_1_out), .sel(whichw));  // open: en
  BlockTop blocktop_1 (
    .in_1(blackbox_1_out_5), .in_2(blackbox_1_out_6), .in_3(blackbox_1_out_7), .in_4(blackbox_1_out_8),
    .out_5(blocktop_1_out_5), .out_13(blocktop_1_out_13), .out_14(blocktop_1_out_14),
    .out_6(blocktop_1_out_6), .out_7(blocktop_1_out_7), .out_15(blocktop_1_out_15),
    .out_16(blocktop_1_out_16), .out_8(blocktop_1_out_8), .out_9(blocktop_1_out_9),
    .out_17(blocktop_1_out_17), .out_18(blocktop_1_out_18), .out_10(blocktop_1_out_10),
    .out_11(blocktop_1_out_11), .out_19(blocktop_1_out_19), .out_20(blocktop_1_out_20),
    .out_12(blocktop_1_out_12));
  _7_Segment_Display u_7_segment_display_3 (
    .g(blocktop_1_out_7), .f(blocktop_1_out_15), .a(blocktop_1_out_16), .b(blocktop_1_out_8),
    .e(blockbottom_1_out_15), .d(blockbottom_1_out_7), .c(blockbottom_1_out_8), .dp(blockbottom_1_out_16));
  _7_Segment_Display u_7_segment_display_4 (
    .g(blocktop_1_out_9), .f(blocktop_1_out_17), .a(blocktop_1_out_18), .b(blocktop_1_out_10),
    .e(blockbottom_1_out_17), .d(blockbottom_1_out_9), .c(blockbottom_1_out_10), .dp(blockbottom_1_out_18));
  blackbox blackbox_1 (
    .out_5(blackbox_1_out_5), .out_6(blackbox_1_out_6), .out_7(blackbox_1_out_7), .out_8(blackbox_1_out_8),
    .in_1(bit_extender_1_out), .in_2(bit_extender_3_out), .in_3(bit_extender_5_out), .in_4(bit_extender_7_out));
  assign bit_extender_3_out = {{4{1'b0}}, register_1_q[11:8]};  // Bit_Extender bit_extender_3
  BlockTop blocktop_2 (
    .in_1(blackbox_2_out_5), .in_2(blackbox_2_out_6), .in_3(blackbox_2_out_7), .in_4(blackbox_2_out_8),
    .out_5(blocktop_2_out_5), .out_13(blocktop_2_out_13), .out_14(blocktop_2_out_14),
    .out_6(blocktop_2_out_6), .out_7(blocktop_2_out_7), .out_15(blocktop_2_out_15),
    .out_16(blocktop_2_out_16), .out_8(blocktop_2_out_8), .out_9(blocktop_2_out_9),
    .out_17(blocktop_2_out_17), .out_18(blocktop_2_out_18), .out_10(blocktop_2_out_10),
    .out_11(blocktop_2_out_11), .out_19(blocktop_2_out_19), .out_20(blocktop_2_out_20),
    .out_12(blocktop_2_out_12));
  _7_Segment_Display u_7_segment_display_5 (
    .g(blocktop_2_out_9), .f(blocktop_2_out_17), .a(blocktop_2_out_18), .b(blocktop_2_out_10),
    .e(blockbottom_2_out_17), .d(blockbottom_2_out_9), .c(blockbottom_2_out_10), .dp(blockbottom_2_out_18));
  _7_Segment_Display u_7_segment_display_6 (
    .g(blocktop_2_out_7), .f(blocktop_2_out_15), .a(blocktop_2_out_16), .b(blocktop_2_out_8),
    .e(blockbottom_2_out_15), .d(blockbottom_2_out_7), .c(blockbottom_2_out_8), .dp(blockbottom_2_out_16));
  blackbox blackbox_2 (
    .out_5(blackbox_2_out_5), .out_6(blackbox_2_out_6), .out_7(blackbox_2_out_7), .out_8(blackbox_2_out_8),
    .in_1(bit_extender_2_out), .in_2(bit_extender_4_out), .in_3(bit_extender_6_out), .in_4(bit_extender_8_out));
  assign bit_extender_4_out = {{4{1'b0}}, register_3_q[11:8]};  // Bit_Extender bit_extender_4
  _7_Segment_Display u_7_segment_display_7 (
    .g(blocktop_1_out_11), .f(blocktop_1_out_19), .a(blocktop_1_out_20), .b(blocktop_1_out_12),
    .e(blockbottom_1_out_19), .d(blockbottom_1_out_11), .c(blockbottom_1_out_12), .dp(blockbottom_1_out_20));
  assign bit_extender_5_out = {{4{1'b0}}, register_1_q[7:4]};  // Bit_Extender bit_extender_5
  _7_Segment_Display u_7_segment_display_8 (
    .g(blocktop_2_out_11), .f(blocktop_2_out_19), .a(blocktop_2_out_20), .b(blocktop_2_out_12),
    .e(blockbottom_2_out_19), .d(blockbottom_2_out_11), .c(blockbottom_2_out_12), .dp(blockbottom_2_out_20));
  assign bit_extender_6_out = {{4{1'b0}}, register_3_q[7:4]};  // Bit_Extender bit_extender_6
  assign bit_extender_7_out = {{4{1'b0}}, register_1_q[3:0]};  // Bit_Extender bit_extender_7
  assign bit_extender_8_out = {{4{1'b0}}, register_3_q[3:0]};  // Bit_Extender bit_extender_8
  _7_Segment_Display u_7_segment_display_9 (
    .g(blocktop_3_out_5), .f(blocktop_3_out_13), .a(blocktop_3_out_14), .b(blocktop_3_out_6),
    .e(blockbottom_3_out_13), .d(blockbottom_3_out_5), .c(blockbottom_3_out_6), .dp(blockbottom_3_out_14));
  BlockBottom blockbottom_3 (
    .out_13(blockbottom_3_out_13), .out_5(blockbottom_3_out_5), .out_6(blockbottom_3_out_6),
    .out_14(blockbottom_3_out_14), .out_15(blockbottom_3_out_15), .out_7(blockbottom_3_out_7),
    .out_8(blockbottom_3_out_8), .out_16(blockbottom_3_out_16), .out_17(blockbottom_3_out_17),
    .out_9(blockbottom_3_out_9), .out_10(blockbottom_3_out_10), .out_18(blockbottom_3_out_18),
    .out_19(blockbottom_3_out_19), .out_11(blockbottom_3_out_11), .out_12(blockbottom_3_out_12),
    .out_20(blockbottom_3_out_20), .in_1(blackbox_3_out_5), .in_2(blackbox_3_out_6), .in_3(blackbox_3_out_7),
    .in_4(blackbox_3_out_8));
  assign bit_extender_9_out = {{4{1'b0}}, register_2_q_4};  // Bit_Extender bit_extender_9
  assign bit_extender_10_out = {{4{1'b0}}, register_4_q[15:12]};  // Bit_Extender bit_extender_10
  BlockTop blocktop_3 (
    .in_1(blackbox_3_out_5), .in_2(blackbox_3_out_6), .in_3(blackbox_3_out_7), .in_4(blackbox_3_out_8),
    .out_5(blocktop_3_out_5), .out_13(blocktop_3_out_13), .out_14(blocktop_3_out_14),
    .out_6(blocktop_3_out_6), .out_7(blocktop_3_out_7), .out_15(blocktop_3_out_15),
    .out_16(blocktop_3_out_16), .out_8(blocktop_3_out_8), .out_9(blocktop_3_out_9),
    .out_17(blocktop_3_out_17), .out_18(blocktop_3_out_18), .out_10(blocktop_3_out_10),
    .out_11(blocktop_3_out_11), .out_19(blocktop_3_out_19), .out_20(blocktop_3_out_20),
    .out_12(blocktop_3_out_12));
  _7_Segment_Display u_7_segment_display_10 (
    .g(blocktop_3_out_7), .f(blocktop_3_out_15), .a(blocktop_3_out_16), .b(blocktop_3_out_8),
    .e(blockbottom_3_out_15), .d(blockbottom_3_out_7), .c(blockbottom_3_out_8), .dp(blockbottom_3_out_16));
  _7_Segment_Display u_7_segment_display_11 (
    .g(blocktop_3_out_9), .f(blocktop_3_out_17), .a(blocktop_3_out_18), .b(blocktop_3_out_10),
    .e(blockbottom_3_out_17), .d(blockbottom_3_out_9), .c(blockbottom_3_out_10), .dp(blockbottom_3_out_18));
  blackbox blackbox_3 (
    .out_5(blackbox_3_out_5), .out_6(blackbox_3_out_6), .out_7(blackbox_3_out_7), .out_8(blackbox_3_out_8),
    .in_1(bit_extender_9_out), .in_2(bit_extender_11_out), .in_3(bit_extender_13_out),
    .in_4(bit_extender_15_out));
  assign bit_extender_11_out = {{4{1'b0}}, register_2_q_3};  // Bit_Extender bit_extender_11
  BlockTop blocktop_4 (
    .in_1(blackbox_4_out_5), .in_2(blackbox_4_out_6), .in_3(blackbox_4_out_7), .in_4(blackbox_4_out_8),
    .out_5(blocktop_4_out_5), .out_13(blocktop_4_out_13), .out_14(blocktop_4_out_14),
    .out_6(blocktop_4_out_6), .out_7(blocktop_4_out_7), .out_15(blocktop_4_out_15),
    .out_16(blocktop_4_out_16), .out_8(blocktop_4_out_8), .out_9(blocktop_4_out_9),
    .out_17(blocktop_4_out_17), .out_18(blocktop_4_out_18), .out_10(blocktop_4_out_10),
    .out_11(blocktop_4_out_11), .out_19(blocktop_4_out_19), .out_20(blocktop_4_out_20),
    .out_12(blocktop_4_out_12));
  _7_Segment_Display u_7_segment_display_12 (
    .g(blocktop_4_out_7), .f(blocktop_4_out_15), .a(blocktop_4_out_16), .b(blocktop_4_out_8),
    .e(blockbottom_4_out_15), .d(blockbottom_4_out_7), .c(blockbottom_4_out_8), .dp(blockbottom_4_out_16));
  _7_Segment_Display u_7_segment_display_13 (
    .g(blocktop_4_out_5), .f(blocktop_4_out_13), .a(blocktop_4_out_14), .b(blocktop_4_out_6),
    .e(blockbottom_4_out_13), .d(blockbottom_4_out_5), .c(blockbottom_4_out_6), .dp(blockbottom_4_out_14));
  BlockBottom blockbottom_4 (
    .out_13(blockbottom_4_out_13), .out_5(blockbottom_4_out_5), .out_6(blockbottom_4_out_6),
    .out_14(blockbottom_4_out_14), .out_15(blockbottom_4_out_15), .out_7(blockbottom_4_out_7),
    .out_8(blockbottom_4_out_8), .out_16(blockbottom_4_out_16), .out_17(blockbottom_4_out_17),
    .out_9(blockbottom_4_out_9), .out_10(blockbottom_4_out_10), .out_18(blockbottom_4_out_18),
    .out_19(blockbottom_4_out_19), .out_11(blockbottom_4_out_11), .out_12(blockbottom_4_out_12),
    .out_20(blockbottom_4_out_20), .in_1(blackbox_4_out_5), .in_2(blackbox_4_out_6), .in_3(blackbox_4_out_7),
    .in_4(blackbox_4_out_8));
  blackbox blackbox_4 (
    .out_5(blackbox_4_out_5), .out_6(blackbox_4_out_6), .out_7(blackbox_4_out_7), .out_8(blackbox_4_out_8),
    .in_1(bit_extender_10_out), .in_2(bit_extender_12_out), .in_3(bit_extender_14_out),
    .in_4(bit_extender_16_out));
  assign bit_extender_12_out = {{4{1'b0}}, register_4_q[11:8]};  // Bit_Extender bit_extender_12
  _7_Segment_Display u_7_segment_display_14 (
    .g(blocktop_3_out_11), .f(blocktop_3_out_19), .a(blocktop_3_out_20), .b(blocktop_3_out_12),
    .e(blockbottom_3_out_19), .d(blockbottom_3_out_11), .c(blockbottom_3_out_12), .dp(blockbottom_3_out_20));
  assign bit_extender_13_out = {{4{1'b0}}, register_2_q_2};  // Bit_Extender bit_extender_13
  _7_Segment_Display u_7_segment_display_15 (
    .g(blocktop_4_out_9), .f(blocktop_4_out_17), .a(blocktop_4_out_18), .b(blocktop_4_out_10),
    .e(blockbottom_4_out_17), .d(blockbottom_4_out_9), .c(blockbottom_4_out_10), .dp(blockbottom_4_out_18));
  _7_Segment_Display u_7_segment_display_16 (
    .g(blocktop_4_out_11), .f(blocktop_4_out_19), .a(blocktop_4_out_20), .b(blocktop_4_out_12),
    .e(blockbottom_4_out_19), .d(blockbottom_4_out_11), .c(blockbottom_4_out_12), .dp(blockbottom_4_out_20));
  assign bit_extender_14_out = {{4{1'b0}}, register_4_q[7:4]};  // Bit_Extender bit_extender_14
  assign bit_extender_15_out = {{4{1'b0}}, register_2_q};  // Bit_Extender bit_extender_15
  assign bit_extender_16_out = {{4{1'b0}}, register_4_q[3:0]};  // Bit_Extender bit_extender_16
  Clock #(.highDuration(4), .lowDuration(4)) clock_2 (.out(clock_2_out));
  Clock #(.highDuration(2), .lowDuration(6)) clock_3 (.out(clock_3_out));
  Multiplexer #(.enable("false")) multiplexer_1 (.in0(1'b0), .in1(WEnable), .out(multiplexer_1_out), .sel(xor_1_out));
  xor xor_1 (xor_1_out, clock_2_out, clock_3_out);

  // Notes on the sheet:
  //   DISP[3]
  //   DISP[3]
  //   DISP[1]
  //   DISP[2]
  //   DISP[2]
  //   DISP[1]
  //   DISP[2]
  //   DISP[2]
  //   DISP[0]
  //   Your Display Logic
  //   DISP[0]
  //   Your Display Logic
  //   BlockTop
  //   BlockBottom
  //   BlockTop
  //   BlockBottom
  //   DISP[3]
  //   DISP[2]
  //   DISP[2]
  //   DISP[3]
  //   DISP[2]
  //   DISP[2]
  //   DISP[1]
  //   DISP[0]
  //   Your Display Logic
  //   DISP[1]
  //   DISP[0]
  //   Your Display Logic
  //   BlockTop
  //   BlockBottom
  //   BlockTop
  //   BlockBottom
endmodule

module ConverterTop (
  input  [7:0] in_1,
  output out_2,
  output out_3,
  output out_4,
  output out_5
);

  wire and_1_out, or_1_out;
  wire [7:0] multiplexer_1_out, multiplexer_2_out;
  wire [7:4] multiplexer_3_out;

  Multiplexer #(.select(4), .width(8), .enable("false")) multiplexer_1 (
    .in0(8'h77), .in1(8'h41), .in2(8'h3b), .in3(8'h6b), .in4(8'h4d), .in5(8'h6e), .in6(8'h7e), .in7(8'h43),
    .in8(8'h7f), .in9(8'h6f), .in10(8'h5f), .in11(8'h7c), .in12(8'h36), .in13(8'h79), .in14(8'h3e),
    .in15(8'h1e), .out(multiplexer_1_out), .sel(in_1[3:0]));
  or or_1 (or_1_out, in_1[4], in_1[5], in_1[6], in_1[7]);
  Multiplexer #(.width(8), .enable("false")) multiplexer_2 (
    .in0(multiplexer_1_out), .in1(8'h9b), .out(multiplexer_2_out), .sel(or_1_out));
  and and_1 (and_1_out, in_1[0], in_1[1], in_1[2], in_1[3], in_1[4], in_1[5], in_1[6], in_1[7]);
  Multiplexer #(.width(8), .enable("false")) multiplexer_3 (
    .in0(multiplexer_2_out), .in1({8{1'b0}}), .out({multiplexer_3_out, out_2, out_3, out_4, out_5}),
    .sel(and_1_out));

  // Notes on the sheet:
  //   0
  //   1
  //   2
  //   3
  //   4
  //   5
  //   6
  //   7
  //   8
  //   9
  //   a
  //   b
  //   c
  //   d
  //   e
  //   f
  //   ?
endmodule

module ConverterBottom (
  input  [7:0] in_1,
  output out_2,
  output out_3,
  output out_4,
  output out_5
);

  wire and_1_out, or_1_out;
  wire [3:0] multiplexer_3_out;
  wire [7:0] multiplexer_1_out, multiplexer_2_out;

  Multiplexer #(.select(4), .width(8), .enable("false")) multiplexer_1 (
    .in0(8'h77), .in1(8'h41), .in2(8'h3b), .in3(8'h6b), .in4(8'h4d), .in5(8'h6e), .in6(8'h7e), .in7(8'h43),
    .in8(8'h7f), .in9(8'h6f), .in10(8'h5f), .in11(8'h7c), .in12(8'h36), .in13(8'h79), .in14(8'h3e),
    .in15(8'h1e), .out(multiplexer_1_out), .sel(in_1[3:0]));
  or or_1 (or_1_out, in_1[4], in_1[5], in_1[6], in_1[7]);
  Multiplexer #(.width(8), .enable("false")) multiplexer_2 (
    .in0(multiplexer_1_out), .in1(8'h9b), .out(multiplexer_2_out), .sel(or_1_out));
  and and_1 (and_1_out, in_1[0], in_1[1], in_1[2], in_1[3], in_1[4], in_1[5], in_1[6], in_1[7]);
  Multiplexer #(.width(8), .enable("false")) multiplexer_3 (
    .in0(multiplexer_2_out), .in1({8{1'b0}}), .out({out_5, out_4, out_3, out_2, multiplexer_3_out}),
    .sel(and_1_out));

  // Notes on the sheet:
  //   0
  //   1
  //   2
  //   3
  //   4
  //   5
  //   6
  //   7
  //   8
  //   9
  //   a
  //   b
  //   c
  //   d
  //   e
  //   f
  //   ?
endmodule

module blackbox (
  input  [7:0] in_1,
  input  [7:0] in_2,
  input  [7:0] in_3,
  input  [7:0] in_4,
  output [7:0] out_5,
  output [7:0] out_6,
  output [7:0] out_7,
  output [7:0] out_8
);


  assign out_5 = in_1;
  assign out_6 = in_2;
  assign out_7 = in_3;
  assign out_8 = in_4;
endmodule

module BlockTop (
  input  [7:0] in_1,
  input  [7:0] in_2,
  input  [7:0] in_3,
  input  [7:0] in_4,
  output out_5,
  output out_6,
  output out_7,
  output out_8,
  output out_9,
  output out_10,
  output out_11,
  output out_12,
  output out_13,
  output out_14,
  output out_15,
  output out_16,
  output out_17,
  output out_18,
  output out_19,
  output out_20
);

  ConverterTop convertertop_1 (.in_1(in_1), .out_2(out_5), .out_3(out_13), .out_4(out_14), .out_5(out_6));
  ConverterTop convertertop_2 (.in_1(in_2), .out_2(out_7), .out_3(out_15), .out_4(out_16), .out_5(out_8));
  ConverterTop convertertop_3 (.in_1(in_3), .out_2(out_9), .out_3(out_17), .out_4(out_18), .out_5(out_10));
  ConverterTop convertertop_4 (.in_1(in_4), .out_2(out_11), .out_3(out_19), .out_4(out_20), .out_5(out_12));
endmodule

module BlockBottom (
  input  [7:0] in_1,
  input  [7:0] in_2,
  input  [7:0] in_3,
  input  [7:0] in_4,
  output out_5,
  output out_6,
  output out_7,
  output out_8,
  output out_9,
  output out_10,
  output out_11,
  output out_12,
  output out_13,
  output out_14,
  output out_15,
  output out_16,
  output out_17,
  output out_18,
  output out_19,
  output out_20
);

  ConverterBottom converterbottom_1 (.in_1(in_1), .out_2(out_13), .out_3(out_5), .out_4(out_6), .out_5(out_14));
  ConverterBottom converterbottom_2 (.in_1(in_2), .out_2(out_15), .out_3(out_7), .out_4(out_8), .out_5(out_16));
  ConverterBottom converterbottom_3 (.in_1(in_3), .out_2(out_17), .out_3(out_9), .out_4(out_10), .out_5(out_18));
  ConverterBottom converterbottom_4 (.in_1(in_4), .out_2(out_19), .out_3(out_11), .out_4(out_12), .out_5(out_20));
endmodule
